# Fritzing sketch Useless-Machine-Schematic (saved by Fritzing 0.9.2b)
breadboards: 1

parts:
  Part1 = Arduino Uno (Rev3)
  Q1 = Basic FET P-Channel [package="TO220 [THT]"]
  R1 = Resistor [tolerance=±5% resistance=10k package=THT]
  C1 = Electrolytic Capacitor [capacitance=100µF package="100 mil [THT, electrolytic]"]
  S1 = Toggle Switch [package=THT]
  J1 = Basic Servo
  J2 = Basic Servo

nets:
  N1: Part1.D11_PWM/MOSI, Q1.gate
  N2: Part1.GND, Q1.source, R1.Pin_0
  N3: Part1.D2, R1.Pin_1, S1.L2
  N4: Part1.D5_PWM, J1.pulse
  N5: Part1.D6_PWM, J2.pulse
  VCC: Part1.5V, C1.+, S1.COM, J1.vcc, J2.vcc
  GND: Q1.drain, C1.-, J1.gnd, J2.gnd
